// Logisim project projetoCircuito.circ as structural Verilog: 1 circuit, main circuit main
module main (
  input  in_1
);

  wire and_1_out, and_2_out, and_3_out, and_4_out, and_5_out, and_6_out, and_7_out, and_8_out, and_9_out,
       and_10_out, and_11_out, and_12_out, and_13_out, and_14_out, and_15_out, and_16_out, and_17_out,
       and_18_out, and_19_out, and_20_out, and_21_out, and_22_out, and_23_out, and_24_out, and_25_out,
       and_26_out, and_27_out, and_28_out, and_29_out, and_30_out, and_31_out, and_32_out, and_33_out,
       and_34_out, and_35_out, and_36_out, and_37_out, dipswitch_1_sw1, dipswitch_1_sw2, dipswitch_1_sw3,
       dipswitch_1_sw4, dipswitch_2_sw1, dipswitch_2_sw2, dipswitch_2_sw3, dipswitch_2_sw4, dipswitch_3_sw1,
       dipswitch_3_sw2, dipswitch_3_sw3, dipswitch_3_sw4, not_1_out, not_2_out, not_3_out, not_4_out,
       not_5_out, not_6_out, not_7_out, not_8_out, not_9_out, or_1_out, or_2_out, or_3_out, or_4_out,
       or_5_out, or_6_out, or_7_out, or_8_out, or_9_out, xnor_1_out, xnor_2_out, xnor_3_out, xnor_4_out,
       xnor_5_out, xnor_6_out, xnor_7_out, xnor_8_out;

  DipSwitch #(.number(4)) dipswitch_1 (
    .sw1(dipswitch_1_sw1), .sw2(dipswitch_1_sw2), .sw3(dipswitch_1_sw3), .sw4(dipswitch_1_sw4));
  not not_1 (not_1_out, dipswitch_1_sw1);
  not not_2 (not_2_out, dipswitch_1_sw2);
  not not_3 (not_3_out, dipswitch_1_sw3);
  not not_4 (not_4_out, dipswitch_1_sw4);
  xnor xnor_1 (xnor_1_out, or_1_out, and_18_out);
  and and_1 (and_1_out, not_1_out, dipswitch_1_sw3, dipswitch_1_sw4);
  and and_2 (and_2_out, not_1_out, dipswitch_1_sw2);
  and and_3 (and_3_out, dipswitch_1_sw2, not_4_out);
  and and_4 (and_4_out, dipswitch_1_sw3, not_4_out);
  and and_5 (and_5_out, not_1_out, dipswitch_1_sw2, dipswitch_1_sw3);
  and and_6 (and_6_out, dipswitch_1_sw1, not_2_out, dipswitch_1_sw3);
  and and_7 (and_7_out, dipswitch_1_sw1, dipswitch_1_sw2, not_4_out);
  and and_8 (and_8_out, not_1_out, not_3_out, dipswitch_1_sw4);
  and and_9 (and_9_out, dipswitch_1_sw2, dipswitch_1_sw3, dipswitch_1_sw4);
  and and_10 (and_10_out, dipswitch_1_sw1, not_2_out, dipswitch_1_sw3);
  and and_11 (and_11_out, dipswitch_1_sw1, dipswitch_1_sw2, not_3_out, not_4_out);
  and and_12 (and_12_out, not_3_out, not_4_out);
  and and_13 (and_13_out, dipswitch_1_sw1, not_2_out, not_3_out);
  and and_14 (and_14_out, dipswitch_1_sw1, not_4_out);
  and and_15 (and_15_out, dipswitch_1_sw1, dipswitch_1_sw2, dipswitch_1_sw3);
  xnor xnor_2 (xnor_2_out, or_2_out, and_19_out);
  and and_16 (and_16_out, xnor_1_out, xnor_2_out, xnor_3_out, xnor_4_out);
  or or_1 (or_1_out, and_1_out, and_2_out, and_3_out);
  or or_2 (or_2_out, and_4_out, and_5_out, and_6_out, and_7_out);
  or or_3 (or_3_out, and_8_out, and_9_out, and_10_out, and_11_out);
  or or_4 (or_4_out, and_12_out, and_13_out, and_14_out, and_15_out);
  xnor xnor_3 (xnor_3_out, or_3_out, and_20_out);
  xnor xnor_4 (xnor_4_out, or_4_out, and_21_out);
  not not_5 (not_5_out, or_5_out);
  and and_17 (and_17_out, in_1, not_5_out);
  and and_18 (and_18_out, in_1, dipswitch_3_sw1);
  and and_19 (and_19_out, in_1, dipswitch_3_sw2);
  LED led_1 (.in(and_17_out));
  DipSwitch #(.number(4)) dipswitch_2 (
    .sw1(dipswitch_2_sw1), .sw2(dipswitch_2_sw2), .sw3(dipswitch_2_sw3), .sw4(dipswitch_2_sw4));
  and and_20 (and_20_out, in_1, dipswitch_3_sw3);
  DipSwitch #(.number(4)) dipswitch_3 (
    .sw1(dipswitch_3_sw1), .sw2(dipswitch_3_sw2), .sw3(dipswitch_3_sw3), .sw4(dipswitch_3_sw4));
  or or_5 (or_5_out, and_16_out, and_37_out);
  and and_21 (and_21_out, in_1, dipswitch_3_sw4);
  LED led_2 (.in(or_5_out));
  not not_6 (not_6_out, dipswitch_2_sw1);
  not not_7 (not_7_out, dipswitch_2_sw2);
  not not_8 (not_8_out, dipswitch_2_sw3);
  not not_9 (not_9_out, dipswitch_2_sw4);
  xnor xnor_5 (xnor_5_out, or_6_out, and_18_out);
  and and_22 (and_22_out, not_6_out, dipswitch_2_sw3, dipswitch_2_sw4);
  and and_23 (and_23_out, not_6_out, dipswitch_2_sw2);
  and and_24 (and_24_out, dipswitch_2_sw2, not_9_out);
  and and_25 (and_25_out, dipswitch_2_sw3, not_9_out);
  and and_26 (and_26_out, not_6_out, dipswitch_2_sw2, dipswitch_2_sw3);
  and and_27 (and_27_out, dipswitch_2_sw1, not_7_out, dipswitch_2_sw3);
  and and_28 (and_28_out, dipswitch_2_sw1, dipswitch_2_sw2, not_9_out);
  and and_29 (and_29_out, not_6_out, not_8_out, dipswitch_2_sw4);
  and and_30 (and_30_out, dipswitch_2_sw2, dipswitch_2_sw3, dipswitch_2_sw4);
  and and_31 (and_31_out, dipswitch_2_sw1, not_7_out, dipswitch_2_sw3);
  and and_32 (and_32_out, dipswitch_2_sw1, dipswitch_2_sw2, not_8_out, not_9_out);
  and and_33 (and_33_out, not_8_out, not_9_out);
  and and_34 (and_34_out, dipswitch_2_sw1, not_7_out, not_8_out);
  and and_35 (and_35_out, dipswitch_2_sw1, not_9_out);
  and and_36 (and_36_out, dipswitch_2_sw1, dipswitch_2_sw2, dipswitch_2_sw3);
  xnor xnor_6 (xnor_6_out, or_7_out, and_19_out);
  and and_37 (and_37_out, xnor_5_out, xnor_6_out, xnor_7_out, xnor_8_out);
  or or_6 (or_6_out, and_22_out, and_23_out, and_24_out);
  or or_7 (or_7_out, and_25_out, and_26_out, and_27_out, and_28_out);
  or or_8 (or_8_out, and_29_out, and_30_out, and_31_out, and_32_out);
  or or_9 (or_9_out, and_33_out, and_34_out, and_35_out, and_36_out);
  xnor xnor_7 (xnor_7_out, or_8_out, and_20_out);
  xnor xnor_8 (xnor_8_out, or_9_out, and_21_out);

  // Notes on the sheet:
  //   navio 1
  //   disparar
  //   errou
  //   alvo
  //   acertou
  //   navio 2
endmodule
